# Fritzing sketch Schema (saved by Fritzing 0.9.4)
breadboards: 2

parts:
  Raspberry_Pi_1 = Raspberry Pi 3 [part_number=RPI-3-V1.2]
  PCF8574 = PCF8574 [package="DIP16 [THT]"]
  16x2_LCD = LCD-16X2 [package=lcd-16x2]
  Soil_Moisture_Sensor = Soil Moisture Sensor
  DS1 = DS18B20 1-Wire Temperature Sensor [part_number=DS18B20]
  LDR = Photocell (LDR) [package=THT]
  MCP3008 = MCP3008 [package=dil16]
  Relay_1 = OMRON PCB Power Relay – G5LE [part_number="G5LE-1\r\n" package=THT]
  Heating_Element = Peltier Element
  Relay_2 = OMRON PCB Power Relay – G5LE [part_number="G5LE-1\r\n" package=THT]
  LED_strips = smd LED [color="Red (633nm)" package="0603 [SMD]"]
  Breadboard_power_supply = Breadboard Power Supply Board SMD
  VCC1 = Battery block 9V
  R4 = Resistor [tolerance=±5% resistance=10k package="0805 [SMD]"]
  R5 = Resistor [tolerance=±5% resistance=10k package="0805 [SMD]"]
  R2 = Resistor [tolerance=±5% resistance=330 package="0805 [SMD]"]
  T-cobbler = T Cobbler Plus
  Pump = DC Motor
  Potentiometer = Trimmer Potentiometer [maximum_resistance=10kΩ package=THT]
  R1 = Resistor [tolerance=±5% resistance=220 package=THT]
  R3 = Resistor [tolerance=±5% resistance=4.7k package=THT]
  Relay_3 = OMRON PCB Power Relay – G5LE [part_number="G5LE-1\r\n" package=THT]
  VCC2 = Battery block 9V

nets:
  3V3: Raspberry_Pi_1.3v3, Raspberry_Pi_1.3V3, T-cobbler.3.3V
  N1: Raspberry_Pi_1.GPIO2, T-cobbler.GPIO_2
  N2: Raspberry_Pi_1.GPIO3, T-cobbler.GPIO_3
  N3: Raspberry_Pi_1.GPIO4, DS1.DQ, T-cobbler.GPIO_4, R3.Pin_0
  GND: Raspberry_Pi_1.GND, T-cobbler.GND
  N4: Raspberry_Pi_1.GPIO17, T-cobbler.GPIO_17
  N5: Raspberry_Pi_1.GPIO27, R2.Pin_0, T-cobbler.GPIO_27
  N6: Raspberry_Pi_1.GPIO22, PCF8574.SCL, R5.Pin_1, T-cobbler.GPIO_22
  N7: Raspberry_Pi_1.GPIO10, T-cobbler.GPIO_10
  N8: Raspberry_Pi_1.GPIO9, T-cobbler.GPIO_9
  N9: Raspberry_Pi_1.GPIO11, T-cobbler.GPIO_11
  N10: Raspberry_Pi_1.ID_SD, T-cobbler.ID_SD
  N11: Raspberry_Pi_1.GPIO5, T-cobbler.GPIO_5
  N12: Raspberry_Pi_1.GPIO6, T-cobbler.GPIO_6
  N13: Raspberry_Pi_1.GPIO13, T-cobbler.GPIO_13
  N14: Raspberry_Pi_1.GPIO19, T-cobbler.GPIO_19
  N15: Raspberry_Pi_1.GPIO26, T-cobbler.GPIO_26
  N16: Raspberry_Pi_1.GPIO21, T-cobbler.GPIO_21
  N17: Raspberry_Pi_1.GPIO20, T-cobbler.GPIO_20
  N18: Raspberry_Pi_1.GPIO16, T-cobbler.GPIO_16
  N19: Raspberry_Pi_1.GPIO12, T-cobbler.GPIO_12
  N20: Raspberry_Pi_1.ID_SC, T-cobbler.ID_SC
  N21: Raspberry_Pi_1.GPIO7, T-cobbler.GPIO_7
  N22: Raspberry_Pi_1.GPIO8, T-cobbler.GPIO_8
  N23: Raspberry_Pi_1.GPIO25, T-cobbler.GPIO_25, Relay_3.COIL2
  N24: Raspberry_Pi_1.GPIO24, Relay_2.COIL2, T-cobbler.GPIO_24
  N25: Raspberry_Pi_1.GPIO23, Relay_1.COIL2, T-cobbler.GPIO_23
  N26: Raspberry_Pi_1.GPIO18, T-cobbler.GPIO_18
  N27: Raspberry_Pi_1.GPIO15, T-cobbler.GPIO_15
  N28: Raspberry_Pi_1.GPIO14, T-cobbler.GPIO_14
  5V: Raspberry_Pi_1.5V, T-cobbler.5V
  GND_2: PCF8574.A0, PCF8574.A1, PCF8574.A2, PCF8574.GND, 16x2_LCD.VSS, 16x2_LCD.K, Soil_Moisture_Sensor.GND, DS1.GND, MCP3008.DGND, MCP3008.AGND, Relay_1.COIL1, Relay_1.C, Relay_2.COIL1, Relay_2.C, Breadboard_power_supply.GND, VCC1.-, Potentiometer.leg1, R1.Pin_1, Relay_3.COIL1, Relay_3.C, VCC2.-
  N29: PCF8574.P0, 16x2_LCD.RS
  N30: PCF8574.P1, 16x2_LCD.R_W
  N31: PCF8574.P2, 16x2_LCD.E
  N32: PCF8574.P4, 16x2_LCD.DB4
  N33: PCF8574.P5, 16x2_LCD.DB5
  N34: PCF8574.P6, 16x2_LCD.DB6
  N35: PCF8574.P7, 16x2_LCD.DB7
  N36: PCF8574.SDA, R4.Pin_1
  VCC: PCF8574.VCC, 16x2_LCD.VDD, 16x2_LCD.A, Soil_Moisture_Sensor.VCC, DS1.VDD, LDR.pin_0, MCP3008.VREF, MCP3008.VDD, Breadboard_power_supply.VCC, R4.Pin_0, R5.Pin_0, R2.Pin_1, Potentiometer.leg2, R3.Pin_1
  N37: 16x2_LCD.VO, Potentiometer.wiper
  N38: Soil_Moisture_Sensor.SIG, MCP3008.CH0
  N39: LDR.pin_1, MCP3008.CH1, R1.Pin_0
  N40: Relay_1.B, Pump.pin_1
  N41: Heating_Element.pin1, Relay_2.B
  N42: Heating_Element.pin2, LED_strips.anode, Breadboard_power_supply.VIN, VCC1.+, Pump.pin_2, VCC2.+
  N43: LED_strips.cathode, Relay_3.B

custom parts:
  T Cobbler Plus: The T-Cobbler Plus is an add on prototyping board from Adafruit specifically designed for the Raspberry Pi B+ that can break out all those tasty power, GPIO, I2C and SPI pins from the 40-pin header onto a solderless breadboard. This set will make "cobbling together" prototypes with the Pi super easy. The T-Cobbler Plus can plug into any solderless breadboard.
